// Logisim project display_picture_12.circ as structural Verilog: 18 circuits, main circuit COMPUTER
module main (
);

  wire CLK_out, RST_out;
  wire [4:0] rgb_video_1_p4, rgb_video_1_p5;
  wire [15:0] computer_1_port_output, undriven;
  wire [23:0] rgb_video_1_p6;

  Button RST (.out(RST_out));
  Clock CLK (.out(CLK_out));
  COMPUTER computer_1 (
    .PORT_OUTPUT(computer_1_port_output), .PIN_INPUT(undriven), .RST(RST_out), .CLK(CLK_out));  // open: KBD
  // RGB_Video #(.height(32), .scale(8), .width(32)) rgb_video_1: pin names not known; wires that end beside it: RST_out, CLK_out, CLK_out, rgb_video_1_p4, rgb_video_1_p5, rgb_video_1_p6
  SCREEN_DRIVER screen_driver_1 (
    .SCREEN_INSTRUCTION(computer_1_port_output), .RGB_COLOR(rgb_video_1_p6), .Y(rgb_video_1_p5),
    .X(rgb_video_1_p4));
endmodule

module COMPUTER (
  input  [15:0] PIN_INPUT,
  input  [6:0] KBD,
  input  RST,
  input  CLK,
  output [15:0] PORT_OUTPUT
);

  wire cpu_1_write_m, cpu_1_write_s, memory_1_cnt_changed, or_1_out, timer_1_interrupt, timer_1_pre_interrupt;
  wire [14:0] cpu_1_address_m, cpu_1_out_pc, cpu_1_out_sp;
  wire [15:0] bit_extender_1_out, cpu_1_out_m, cpu_1_out_s, memory_1_cnt_out, memory_1_ddr_out,
       memory_1_mask_out, memory_1_out_m, memory_1_out_s, memory_1_port_out, memory_1_prescaler_out,
       port_controller_1_pin_out, rom_1_data, timer_1_counter_val;

  ROM #(.addrWidth(15), .dataWidth(16)) rom_1 (.addr(cpu_1_out_pc), .data(rom_1_data));
  CPU cpu_1 (
    .WRITE_S(cpu_1_write_s), .OUT_SP(cpu_1_out_sp), .OUT_M(cpu_1_out_m), .WRITE_M(cpu_1_write_m),
    .ADDRESS_M(cpu_1_address_m), .OUT_PC(cpu_1_out_pc), .OUT_S(cpu_1_out_s), .RESET(RST), .CLK(CLK),
    .INTERRUPT(timer_1_interrupt), .IN_M(memory_1_out_m), .IN_S(memory_1_out_s),
    .PRE_INTERRUPT(timer_1_pre_interrupt), .INSTRUCTION(rom_1_data));
  or or_1 (or_1_out, timer_1_interrupt, CLK);
  MEMORY memory_1 (
    .OUT_M(memory_1_out_m), .DDR_OUT(memory_1_ddr_out), .PORT_OUT(memory_1_port_out),
    .MASK_OUT(memory_1_mask_out), .PRESCALER_OUT(memory_1_prescaler_out), .CNT_OUT(memory_1_cnt_out),
    .CNT_CHANGED(memory_1_cnt_changed), .OUT_S(memory_1_out_s), .PIN_IN(port_controller_1_pin_out),
    .CNT_IN(timer_1_counter_val), .KBD_IN(bit_extender_1_out), .WRITE_M(cpu_1_write_m),
    .WRITE_S(cpu_1_write_s), .CLK(or_1_out), .IN_M(cpu_1_out_m), .ADDRESS_M(cpu_1_address_m),
    .IN_S(cpu_1_out_s), .ADDRESS_S(cpu_1_out_sp));
  PORT_CONTROLLER port_controller_1 (
    .PIN_OUT(port_controller_1_pin_out), .PORT_OUT(PORT_OUTPUT), .DDR_IN(memory_1_ddr_out),
    .PORT_IN(memory_1_port_out), .PIN_IN(PIN_INPUT));
  TIMER timer_1 (
    .INTERRUPT(timer_1_interrupt), .COUNTER_VAL(timer_1_counter_val), .PRE_INTERRUPT(timer_1_pre_interrupt),
    .CNT_CHANGED(memory_1_cnt_changed), .CLK(CLK), .MASK(memory_1_mask_out),
    .PRESCALER(memory_1_prescaler_out), .CNT_IN(memory_1_cnt_out));
  assign bit_extender_1_out = {{9{1'b0}}, KBD};  // Bit_Extender bit_extender_1
  LED led_1 (.in(PORT_OUTPUT[15]));
  LED led_2 (.in(PORT_OUTPUT[14]));
  LED led_3 (.in(PORT_OUTPUT[13]));
  LED led_4 (.in(PORT_OUTPUT[12]));
  LED led_5 (.in(PORT_OUTPUT[11]));
  LED led_6 (.in(PORT_OUTPUT[10]));
  LED led_7 (.in(PORT_OUTPUT[9]));
  LED led_8 (.in(PORT_OUTPUT[8]));
  LED led_9 (.in(PORT_OUTPUT[7]));
  LED led_10 (.in(PORT_OUTPUT[6]));
  LED led_11 (.in(PORT_OUTPUT[5]));
  LED led_12 (.in(PORT_OUTPUT[4]));
  LED led_13 (.in(PORT_OUTPUT[3]));
  LED led_14 (.in(PORT_OUTPUT[2]));
  LED led_15 (.in(PORT_OUTPUT[1]));
  LED led_16 (.in(PORT_OUTPUT[0]));

  // Notes on the sheet:
  //   contents of rom_1 (hex, n*v repeats v):
  //   40 8088 0 8848 3f c040 40 8088 20 8848 3f c040 40 8088 40 8848 3f c040 40 8088 60 8848 3f c040 40
  //   8088 80 8848 3f c040 40 8088 a0 8848 3f c040 40 8088 c0 8848 3f c040 40 8088 e0 8848 3f c040 40 8088
  //   100 8848 3f c040 40 8088 120 8848 3f c040 40 8088 140 8848 3f c040 40 8088 160 8848 3f c040 40 8088
  //   180 8848 3f c040 40 8088 1a0 8848 3f c040 40 8088 1c0 8848 3f c040 40 8088 1e0 8848 3f c040 40 8088
  //   200 8848 3f c040 40 8088 220 8848 3f c040 40 8088 240 8848 3f c040 40 8088 260 8848 3f c040 40 8088
  //   280 8848 3f c040 40 8088 2a0 8848 3f c040 40 8088 2c0 8848 3f c040 40 8088 2e0 8848 3f c040 40 8088
  //   300 8848 3f c040 40 8088 320 8848 3f c040 40 8088 340 8848 3f c040 40 8088 360 8848 3f c040 40 8088
  //   380 8848 3f c040 40 8088 3a0 8848 3f c040 40 8088 3c0 8848 3f c040 40 8088 3e0 8848 3f c040 40 8088
  //   1 8848 3f c040 40 8088 21 8848 3f c040 40 8088 41 8848 3f c040 40 8088 61 8848 3f c040 40 8088 81
  //   8848 3f c040 40 8088 a1 8848 3f c040 40 8088 c1 8848 3f c040 40 8088 e1 8848 3f c040 40 8088 101
  //   8848 3f c040 40 8088 121 8848 3f c040 40 8088 141 8848 3f c040 40 8088 161 8848 3f c040 40 8088 181
  //   8848 3f c040 40 8088 1a1 8848 3f c040 40 8088 1c1 8848 3f c040 40 8088 1e1 8848 3f c040 40 8088 201
  //   8848 3f c040 40 8088 221 8848 3f c040 40 8088 241 8848 3f c040 40 8088 261 8848 3f c040 40 8088 281
  //   8848 3f c040 40 8088 2a1 8848 3f c040 40 8088 2c1 8848 3f c040 40 8088 2e1 8848 3f c040 40 8088 301
  //   8848 3f c040 40 8088 321 8848 3f c040 40 8088 341 8848 3f c040 40 8088 361 8848 3f c040 40 8088 381
  //   8848 3f c040 40 8088 3a1 8848 3f c040 40 8088 3c1 8848 3f c040 40 8088 3e1 8848 3f c040 40 8088 2
  //   8848 3f c040 40 8088 22 8848 3f c040 40 8088 42 8848 3f c040 40 8088 62 8848 3f c040 40 8088 82 8848
  //   3f c040 40 8088 a2 8848 3f c040 40 8088 c2 8848 3f c040 40 8088 e2 8848 3f c040 40 8088 102 8848 3f
  //   c040 40 8088 122 8848 3f c040 40 8088 142 8848 3f c040 40 8088 162 8848 3f c040 40 8088 182 8848 3f
  //   c040 40 8088 1a2 8848 3f c040 40 8088 1c2 8848 3f c040 40 8088 1e2 8848 3f c040 40 8088 202 8848 3f
  //   c040 40 8088 222 8848 3f c040 40 8088 242 8848 3f c040 40 8088 262 8848 3f c040 40 8088 282 8848 3f
  //   c040 40 8088 2a2 8848 3f c040 40 8088 2c2 8848 3f c040 40 8088 2e2 8848 3f c040 40 8088 302 8848 3f
  //   c040 40 8088 322 8848 3f c040 40 8088 342 8848 3f c040 40 8088 362 8848 3f c040 40 8088 382 8848 3f
  //   c040 40 8088 3a2 8848 3f c040 40 8088 3c2 8848 3f c040 40 8088 3e2 8848 3f c040 40 8088 3 8848 3f
  //   c040 40 8088 23 8848 3f c040 40 8088 43 8848 3f c040 40 8088 63 8848 3f c040 40 8088 83 8848 3f c040
  //   40 8088 a3 8848 3f c040 40 8088 c3 8848 3f c040 40 8088 e3 8848 3f c040 40 8088 103 8848 3f c040 40
  //   8088 123 8848 3f c040 40 8088 143 8848 3f c040 40 8088 163 8848 3f c040 40 8088 183 8848 3f c040 40
  //   8088 1a3 8848 3f c040 40 8088 1c3 8848 3f c040 40 8088 1e3 8848 20 c040 40 8088 203 8848 20 c040 40
  //   8088 223 8848 20 c040 40 8088 243 8848 30 c040 40 8088 263 8848 30 c040 40 8088 283 8848 30 c040 40
  //   8088 2a3 8848 30 c040 40 8088 2c3 8848 3f c040 40 8088 2e3 8848 3f c040 40 8088 303 8848 3f c040 40
  //   8088 323 8848 3f c040 40 8088 343 8848 3f c040 40 8088 363 8848 3f c040 40 8088 383 8848 3f c040 40
  //   8088 3a3 8848 3f c040 40 8088 3c3 8848 3f c040 40 8088 3e3 8848 3f c040 40 8088 4 8848 3f c040 40
  //   8088 24 8848 3f c040 40 8088 44 8848 3f c040 40 8088 64 8848 3f c040 40 8088 84 8848 3f c040 40 8088
  //   a4 8848 3f c040 40 8088 c4 8848 3f c040 40 8088 e4 8848 3f c040 40 8088 104 8848 3f c040 40 8088 124
  //   8848 3f c040 40 8088 144 8848 3f c040 40 8088 164 8848 3f c040 40 8088 184 8848 3f c040 40 8088 1a4
  //   8848 20 c040 40 8088 1c4 8848 20 c040 40 8088 1e4 8848 20 c040 40 8088 204 8848 20 c040 40 8088 224
  //   8848 20 c040 40 8088 244 8848 20 c040 40 8088 264 8848 20 c040 40 8088 284 8848 20 c040 40 8088 2a4
  //   8848 20 c040 40 8088 2c4 8848 30 c040 40 8088 2e4 8848 3a c040 40 8088 304 8848 3f c040 40 8088 324
  //   8848 3f c040 40 8088 344 8848 3f c040 40 8088 364 8848 3f c040 40 8088 384 8848 3f c040 40 8088 3a4
  //   8848 3f c040 40 8088 3c4 8848 3f c040 40 8088 3e4 8848 3f c040 40 8088 5 8848 3f c040 40 8088 25
  //   8848 3f c04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
endmodule

module CPU (
  input  [15:0] INSTRUCTION,
  input  [15:0] IN_M,
  input  [15:0] IN_S,
  input  RESET,
  input  CLK,
  input  INTERRUPT,
  input  PRE_INTERRUPT,
  output [15:0] OUT_M,
  output WRITE_M,
  output [14:0] ADDRESS_M,
  output [14:0] OUT_PC,
  output WRITE_S,
  output [14:0] OUT_SP,
  output [15:0] OUT_S
);

  wire and_1_out, and_2_out, and_3_out, and_4_out, and_5_out, and_6_out, and_7_out, c_inst_parser_1_a,
       c_inst_parser_1_a_m, c_inst_parser_1_d, c_inst_parser_1_m, c_inst_parser_1_pp, c_inst_parser_1_s,
       inst_type_1_a, inst_type_1_c, jump_decider_1_jmp_bool, not_1_out, or_1_out, or_2_out, or_3_out;
  wire [2:0] c_inst_parser_1_jmp, c_inst_parser_1_oprnd, c_inst_parser_1_oprtr;
  wire [14:0] bit_extender_1_out, sc_1_sp;
  wire [15:0] D_q, multiplexer_1_out, multiplexer_2_out, multiplexer_3_out, multiplexer_4_out,
       multiplexer_5_out, selector_1_out1, selector_1_out2;
  wire [15:15] A_q, pc_1_out1;

  Multiplexer #(.enable("false"), .width(16)) multiplexer_1 (
    .in0(INSTRUCTION), .in1({16{1'b0}}), .out(multiplexer_1_out), .sel(PRE_INTERRUPT));
  or or_1 (or_1_out, RESET, INTERRUPT);
  Multiplexer #(.enable("false"), .width(16)) multiplexer_2 (
    .in0(multiplexer_1_out), .in1(OUT_M), .out(multiplexer_2_out), .sel(inst_type_1_c));
  C_INST_PARSER c_inst_parser_1 (
    .D(c_inst_parser_1_d), .M(c_inst_parser_1_m), .A(c_inst_parser_1_a), .A_M(c_inst_parser_1_a_m),
    .PP(c_inst_parser_1_pp), .S(c_inst_parser_1_s), .OPRND(c_inst_parser_1_oprnd),
    .OPRTR(c_inst_parser_1_oprtr), .JMP(c_inst_parser_1_jmp), .INSTRUCTION(multiplexer_1_out));
  INST_TYPE inst_type_1 (.A(inst_type_1_a), .C(inst_type_1_c), .INSTRUCTION(multiplexer_1_out));
  and and_1 (and_1_out, c_inst_parser_1_a, inst_type_1_c);
  and and_2 (and_2_out, c_inst_parser_1_d, inst_type_1_c);
  or or_2 (or_2_out, and_1_out, inst_type_1_a);
  Register #(.width(16)) A (.D(multiplexer_2_out), .en(and_3_out), .clk(CLK), .Q({A_q[15], ADDRESS_M}), .clr(RESET));
  and and_3 (and_3_out, or_2_out, ~PRE_INTERRUPT);  // AND_Gate
  or or_3 (or_3_out, c_inst_parser_1_s, PRE_INTERRUPT);
  Register #(.width(16)) D (.D(OUT_M), .en(and_2_out), .clk(CLK), .Q(D_q), .clr(RESET));
  and and_4 (and_4_out, c_inst_parser_1_s, c_inst_parser_1_pp);
  Multiplexer #(.enable("false"), .width(16)) multiplexer_3 (
    .in0({A_q[15], ADDRESS_M}), .in1(IN_M), .out(multiplexer_3_out), .sel(c_inst_parser_1_a_m));
  Multiplexer #(.enable("false"), .width(16)) multiplexer_4 (
    .in0(multiplexer_3_out), .in1(IN_S), .out(multiplexer_4_out), .sel(and_4_out));
  Multiplexer #(.enable("false"), .width(16)) multiplexer_5 (
    .in0({A_q[15], ADDRESS_M}), .in1(OUT_M), .out(multiplexer_5_out), .sel(c_inst_parser_1_a));
  SC sc_1 (.SP(sc_1_sp), .CLK(CLK), .RESET(RESET), .PUSH_POP(c_inst_parser_1_pp), .ENABLE(or_3_out));
  JUMP_DECIDER jump_decider_1 (.JMP_BOOL(jump_decider_1_jmp_bool), .ALU_OUT(OUT_M), .JMP_SEL(c_inst_parser_1_jmp));
  SELECTOR selector_1 (
    .OUT1(selector_1_out1), .OUT2(selector_1_out2), .OPERAND_SEL(c_inst_parser_1_oprnd), .D(D_q),
    .A(multiplexer_4_out));
  and and_5 (and_5_out, jump_decider_1_jmp_bool, inst_type_1_c);
  not not_1 (not_1_out, c_inst_parser_1_pp);
  and and_6 (and_6_out, inst_type_1_c, not_1_out, c_inst_parser_1_s);
  and and_7 (and_7_out, inst_type_1_c, c_inst_parser_1_pp, c_inst_parser_1_s);
  PC pc_1 (.OUT1({pc_1_out1[15], OUT_PC}), .LOAD(and_5_out), .RESET(or_1_out), .CLK(CLK), .IN1(multiplexer_5_out));
  assign bit_extender_1_out = {{14{1'b0}}, and_7_out};  // Bit_Extender bit_extender_1
  and and_8 (WRITE_M, c_inst_parser_1_m, inst_type_1_c);
  ALU alu_1 (.OUT1(OUT_M), .IN1(selector_1_out1), .IN2(selector_1_out2), .SEL(c_inst_parser_1_oprtr));
  Subtractor #(.width(15)) subtractor_1 (.a(sc_1_sp), .b(bit_extender_1_out), .out(OUT_SP));  // open: bin, bout
  or or_4 (WRITE_S, and_6_out, PRE_INTERRUPT);
  Multiplexer #(.enable("false"), .width(16)) multiplexer_6 (
    .in0(OUT_M), .in1({pc_1_out1[15], OUT_PC}), .out(OUT_S), .sel(PRE_INTERRUPT));
endmodule

module ALU (
  input  [15:0] IN1,
  input  [15:0] IN2,
  input  [2:0] SEL,
  output [15:0] OUT1
);

  wire [15:0] adder_1_out, and_1_out, divider_1_out, multiplier_1_out, not_1_out, or_1_out, subtractor_1_out,
       xor_1_out;

  Adder #(.width(16)) adder_1 (.a(IN1), .b(IN2), .out(adder_1_out));  // open: cin, cout
  Subtractor #(.width(16)) subtractor_1 (.a(IN1), .b(IN2), .out(subtractor_1_out));  // open: bin, bout
  Multiplier #(.width(16)) multiplier_1 (.a(IN1), .b(IN2), .out(multiplier_1_out));  // open: cin, cout
  Divider #(.width(16)) divider_1 (.a(IN1), .b(IN2), .out(divider_1_out));  // open: upper, rem
  assign not_1_out = ~IN2;  // NOT_Gate not_1, 16 bits wide
  assign and_1_out = IN1 & IN2;  // AND_Gate and_1, 16 bits wide
  assign or_1_out = IN1 | IN2;  // OR_Gate or_1, 16 bits wide
  assign xor_1_out = IN1 ^ IN2;  // XOR_Gate xor_1, 16 bits wide
  Multiplexer #(.enable("false"), .select(3), .width(16)) multiplexer_1 (
    .in0(adder_1_out), .in1(subtractor_1_out), .in2(multiplier_1_out), .in3(divider_1_out), .in4(not_1_out),
    .in5(and_1_out), .in6(or_1_out), .in7(xor_1_out), .out(OUT1), .sel(SEL));
endmodule

module PC (
  input  LOAD,
  input  RESET,
  input  CLK,
  input  [15:0] IN1,
  output [15:0] OUT1
);

  Counter #(.max('hffff), .width(16)) counter_1 (
    .clr(RESET), .load(LOAD), .up(1'b1), .count(1'b1), .clk(CLK), .D(IN1), .Q(OUT1));  // open: carry
endmodule

module SELECTOR (
  input  [15:0] D,
  input  [15:0] A,
  input  [2:0] OPERAND_SEL,
  output [15:0] OUT1,
  output [15:0] OUT2
);

  Multiplexer #(.enable("false"), .select(3), .width(16)) multiplexer_1 (
    .in0({16{1'b0}}), .in1(D), .in2({16{1'b0}}), .in3({16{1'b0}}), .in4(A), .in5({16{1'b0}}), .in6(A),
    .in7(D), .out(OUT1), .sel(OPERAND_SEL));
  Multiplexer #(.enable("false"), .select(3), .width(16)) multiplexer_2 (
    .in0({16{1'b0}}), .in1(A), .in2(A), .in3(D), .in4(D), .in5(16'h1), .in6(16'h1), .in7(16'h1), .out(OUT2),
    .sel(OPERAND_SEL));
endmodule

module INST_TYPE (
  input  [15:0] INSTRUCTION,
  output A,
  output C
);

  not not_1 (A, INSTRUCTION[15]);

  assign C = INSTRUCTION[15];
endmodule

module C_INST_PARSER (
  input  [15:0] INSTRUCTION,
  output [2:0] JMP,
  output D,
  output M,
  output A,
  output [2:0] OPRND,
  output A_M,
  output [2:0] OPRTR,
  output PP,
  output S
);


  assign A = INSTRUCTION[5];
  assign A_M = INSTRUCTION[9];
  assign D = INSTRUCTION[3];
  assign JMP = INSTRUCTION[2:0];
  assign M = INSTRUCTION[4];
  assign OPRND = INSTRUCTION[8:6];
  assign OPRTR = INSTRUCTION[12:10];
  assign PP = INSTRUCTION[13];
  assign S = INSTRUCTION[14];
endmodule

module JUMP_DECIDER (
  input  [2:0] JMP_SEL,
  input  [15:0] ALU_OUT,
  output JMP_BOOL
);

  wire and_1_out, and_2_out, and_3_out, comparator_1_eq, comparator_1_gt, comparator_1_lt;

  Comparator #(.width(16)) comparator_1 (
    .a(ALU_OUT), .b({16{1'b0}}), .gt(comparator_1_gt), .eq(comparator_1_eq), .lt(comparator_1_lt));
  and and_1 (and_1_out, JMP_SEL[0], comparator_1_gt);
  and and_2 (and_2_out, comparator_1_eq, JMP_SEL[1]);
  and and_3 (and_3_out, comparator_1_lt, JMP_SEL[2]);
  or or_1 (JMP_BOOL, and_1_out, and_2_out, and_3_out);
endmodule

module DELAY (
  input  IN1,
  output out_2
);

  wire not_1_out, not_2_out, not_3_out, not_4_out, not_5_out, not_6_out, not_7_out, not_8_out, not_9_out,
       not_10_out, not_11_out, not_12_out, not_13_out, not_14_out, not_15_out, not_16_out, not_17_out,
       not_18_out, not_19_out, not_20_out, not_21_out, not_22_out, not_23_out, not_24_out, not_25_out,
       not_26_out, not_27_out, not_28_out, not_29_out, not_30_out, not_31_out, not_32_out, not_33_out,
       not_34_out, not_35_out, not_36_out, not_37_out, not_38_out, not_39_out, not_40_out, not_41_out,
       not_42_out, not_43_out, not_44_out, not_45_out, not_46_out, not_47_out, not_48_out, not_49_out,
       not_50_out, not_51_out, not_52_out, not_53_out, not_54_out, not_55_out, not_56_out, not_57_out,
       not_58_out, not_59_out, not_60_out, not_61_out, not_62_out, not_63_out;

  not not_1 (not_1_out, IN1);
  not not_2 (not_2_out, not_1_out);
  not not_3 (not_3_out, not_63_out);
  not not_4 (not_4_out, not_3_out);
  not not_5 (not_5_out, not_2_out);
  not not_6 (not_6_out, not_5_out);
  not not_7 (not_7_out, not_4_out);
  not not_8 (not_8_out, not_7_out);
  not not_9 (not_9_out, not_6_out);
  not not_10 (not_10_out, not_9_out);
  not not_11 (not_11_out, not_10_out);
  not not_12 (not_12_out, not_8_out);
  not not_13 (not_13_out, not_12_out);
  not not_14 (not_14_out, not_13_out);
  not not_15 (not_15_out, not_11_out);
  not not_16 (not_16_out, not_15_out);
  not not_17 (not_17_out, not_16_out);
  not not_18 (not_18_out, not_14_out);
  not not_19 (not_19_out, not_18_out);
  not not_20 (not_20_out, not_19_out);
  not not_21 (not_21_out, not_17_out);
  not not_22 (not_22_out, not_21_out);
  not not_23 (not_23_out, not_20_out);
  not not_24 (not_24_out, not_23_out);
  not not_25 (not_25_out, not_22_out);
  not not_26 (not_26_out, not_25_out);
  not not_27 (not_27_out, not_26_out);
  not not_28 (not_28_out, not_24_out);
  not not_29 (not_29_out, not_28_out);
  not not_30 (not_30_out, not_29_out);
  not not_31 (not_31_out, not_27_out);
  not not_32 (not_32_out, not_31_out);
  not not_33 (not_33_out, not_32_out);
  not not_34 (not_34_out, not_30_out);
  not not_35 (not_35_out, not_34_out);
  not not_36 (not_36_out, not_35_out);
  not not_37 (not_37_out, not_33_out);
  not not_38 (not_38_out, not_37_out);
  not not_39 (not_39_out, not_36_out);
  not not_40 (not_40_out, not_39_out);
  not not_41 (not_41_out, not_38_out);
  not not_42 (not_42_out, not_41_out);
  not not_43 (not_43_out, not_42_out);
  not not_44 (not_44_out, not_40_out);
  not not_45 (not_45_out, not_44_out);
  not not_46 (not_46_out, not_45_out);
  not not_47 (not_47_out, not_43_out);
  not not_48 (not_48_out, not_47_out);
  not not_49 (not_49_out, not_48_out);
  not not_50 (not_50_out, not_46_out);
  not not_51 (not_51_out, not_50_out);
  not not_52 (not_52_out, not_51_out);
  not not_53 (not_53_out, not_54_out);
  not not_54 (not_54_out, not_49_out);
  not not_55 (not_55_out, not_56_out);
  not not_56 (not_56_out, not_52_out);
  not not_57 (not_57_out, not_53_out);
  not not_58 (not_58_out, not_57_out);
  not not_59 (not_59_out, not_58_out);
  not not_60 (not_60_out, not_55_out);
  not not_61 (not_61_out, not_60_out);
  not not_62 (not_62_out, not_61_out);
  not not_63 (not_63_out, not_59_out);
  not not_64 (out_2, not_62_out);
endmodule

module SC (
  input  RESET,
  input  PUSH_POP,
  input  ENABLE,
  input  CLK,
  output [14:0] SP
);

  wire not_1_out;

  Counter #(.max('h7fff), .width(15)) counter_1 (
    .clr(RESET), .up(not_1_out), .count(ENABLE), .clk(CLK), .Q(SP));  // open: load, D, carry
  not not_1 (not_1_out, PUSH_POP);
endmodule

module MEMORY (
  input  [15:0] PIN_IN,
  input  [15:0] CNT_IN,
  input  [15:0] KBD_IN,
  input  [15:0] IN_M,
  input  WRITE_M,
  input  [14:0] ADDRESS_M,
  input  [15:0] IN_S,
  input  WRITE_S,
  input  [14:0] ADDRESS_S,
  input  CLK,
  output [15:0] OUT_M,
  output [15:0] DDR_OUT,
  output [15:0] PORT_OUT,
  output [15:0] MASK_OUT,
  output [15:0] PRESCALER_OUT,
  output [15:0] CNT_OUT,
  output CNT_CHANGED,
  output [15:0] OUT_S
);

  wire comparator_1_eq, memwrite_controller_1_write_ddr, memwrite_controller_1_write_mask,
       memwrite_controller_1_write_port, memwrite_controller_1_write_prescaler,
       memwrite_controller_1_write_ram, not_1_out, undriven;
  wire [14:0] memwrite_controller_1_address_ram;
  wire [15:0] COUNTER_REG_q, KBD_REG_q, PIN_REG_q, ram_1_dout;

  MEMWRITE_CONTROLLER memwrite_controller_1 (
    .WRITE_M(WRITE_M), .ADDRESS_M(ADDRESS_M), .WRITE_DDR(memwrite_controller_1_write_ddr),
    .WRITE_PORT(memwrite_controller_1_write_port), .WRITE_MASK(memwrite_controller_1_write_mask),
    .WRITE_PRESCALER(memwrite_controller_1_write_prescaler), .WRITE_COUNTER(CNT_CHANGED),
    .ADDRESS_RAM(memwrite_controller_1_address_ram), .WRITE_RAM(memwrite_controller_1_write_ram));  // open: WRITE_PIN, WRITE_KBD
  Register #(.width(16)) DDR_REG (.D(IN_M), .en(memwrite_controller_1_write_ddr), .clk(CLK), .Q(DDR_OUT));  // open: clr
  Register #(.width(16)) PORT_REG (
    .D(IN_M), .en(memwrite_controller_1_write_port), .clk(CLK), .Q(PORT_OUT));  // open: clr
  Register #(.width(16)) PIN_REG (.D(PIN_IN), .en(not_1_out), .clk(not_1_out), .Q(PIN_REG_q));  // open: clr
  Register #(.width(16)) MASK_REG (
    .D(IN_M), .en(memwrite_controller_1_write_mask), .clk(CLK), .Q(MASK_OUT));  // open: clr
  Register #(.width(16)) PRESCALER_REG (
    .D(IN_M), .en(memwrite_controller_1_write_prescaler), .clk(CLK), .Q(PRESCALER_OUT));  // open: clr
  Register #(.width(16)) COUNTER_REG (.D(CNT_OUT), .en(CLK), .clk(CLK), .Q(COUNTER_REG_q));  // open: clr
  Multiplexer #(.enable("false"), .width(16)) multiplexer_1 (
    .in0(CNT_IN), .in1(IN_M), .out(CNT_OUT), .sel(CNT_CHANGED));
  Register #(.width(16)) KBD_REG (.D(KBD_IN), .en(CLK), .clk(CLK), .Q(KBD_REG_q), .clr(undriven));
  RAM #(.addrWidth(15), .dataWidth(16), .enables("line")) ram_1 (
    .addr(memwrite_controller_1_address_ram), .we(memwrite_controller_1_write_ram), .clk(CLK), .din(IN_M),
    .dout(ram_1_dout));
  RAM #(.addrWidth(15), .dataWidth(16), .enables("line")) ram_2 (
    .addr(ADDRESS_S), .we(WRITE_S), .clk(CLK), .din(IN_S), .dout(OUT_S));
  not not_1 (not_1_out, comparator_1_eq);
  Comparator #(.width(16)) comparator_1 (.a(PIN_REG_q), .b(PIN_IN), .eq(comparator_1_eq));  // open: gt, lt
  MEMREAD_CONTROLLER memread_controller_1 (
    .OUT_M(OUT_M), .ADDRESS_M(ADDRESS_M), .DDR_M(DDR_OUT), .PORT_M(PORT_OUT), .PIN_M(PIN_REG_q),
    .MASK_M(MASK_OUT), .PRESCALER_M(PRESCALER_OUT), .COUNTER_M(COUNTER_REG_q), .KBD_M(KBD_REG_q),
    .RAM_M(ram_1_dout));
endmodule

module PORT_CONTROLLER (
  input  [15:0] DDR_IN,
  input  [15:0] PORT_IN,
  input  [15:0] PIN_IN,
  output [15:0] PORT_OUT,
  output [15:0] PIN_OUT
);

  assign PIN_OUT = ~DDR_IN & PIN_IN;  // AND_Gate and_1, 16 bits wide
  assign PORT_OUT = DDR_IN & PORT_IN;  // AND_Gate and_2, 16 bits wide
endmodule

module MEMWRITE_CONTROLLER (
  input  WRITE_M,
  input  [14:0] ADDRESS_M,
  output WRITE_DDR,
  output WRITE_PORT,
  output WRITE_PIN,
  output WRITE_MASK,
  output WRITE_PRESCALER,
  output WRITE_COUNTER,
  output WRITE_KBD,
  output [14:0] ADDRESS_RAM,
  output WRITE_RAM
);

  wire comparator_1_lt;
  wire [2:0] bit_extender_1_out, bit_extender_2_out, multiplexer_1_out;

  Bit_Extender #(.in_width(15), .out_width(3)) bit_extender_1 (.in(ADDRESS_M), .out(bit_extender_1_out));
  Comparator #(.width(15)) comparator_1 (.a(ADDRESS_M), .b(15'h7), .lt(comparator_1_lt));  // open: gt, eq
  Bit_Extender #(.in_width(15), .out_width(3)) bit_extender_2 (.in(15'h7), .out(bit_extender_2_out));
  Subtractor #(.width(15)) subtractor_1 (.a(ADDRESS_M), .b(15'h7), .out(ADDRESS_RAM));  // open: bin, bout
  Multiplexer #(.enable("false"), .width(3)) multiplexer_1 (
    .in0(bit_extender_2_out), .in1(bit_extender_1_out), .out(multiplexer_1_out), .sel(comparator_1_lt));
  Demultiplexer #(.enable("false"), .select(3)) demultiplexer_1 (
    .out0(WRITE_DDR), .out1(WRITE_PORT), .out2(WRITE_PIN), .out3(WRITE_MASK), .out4(WRITE_PRESCALER),
    .out5(WRITE_COUNTER), .out6(WRITE_KBD), .out7(WRITE_RAM), .in(WRITE_M), .sel(multiplexer_1_out));
endmodule

module MEMREAD_CONTROLLER (
  input  [15:0] DDR_M,
  input  [15:0] PORT_M,
  input  [15:0] PIN_M,
  input  [15:0] MASK_M,
  input  [15:0] PRESCALER_M,
  input  [15:0] COUNTER_M,
  input  [15:0] KBD_M,
  input  [15:0] RAM_M,
  input  [14:0] ADDRESS_M,
  output [15:0] OUT_M
);

  wire comparator_1_lt;
  wire [2:0] bit_extender_1_out, bit_extender_2_out, multiplexer_1_out;

  Bit_Extender #(.in_width(15), .out_width(3)) bit_extender_1 (.in(ADDRESS_M), .out(bit_extender_1_out));
  Comparator #(.width(15)) comparator_1 (.a(ADDRESS_M), .b(15'h7), .lt(comparator_1_lt));  // open: gt, eq
  Bit_Extender #(.in_width(15), .out_width(3)) bit_extender_2 (.in(15'h7), .out(bit_extender_2_out));
  Multiplexer #(.enable("false"), .width(3)) multiplexer_1 (
    .in0(bit_extender_2_out), .in1(bit_extender_1_out), .out(multiplexer_1_out), .sel(comparator_1_lt));
  Multiplexer #(.enable("false"), .select(3), .width(16)) multiplexer_2 (
    .in0(DDR_M), .in1(PORT_M), .in2(PIN_M), .in3(MASK_M), .in4(PRESCALER_M), .in5(COUNTER_M), .in6(KBD_M),
    .in7(RAM_M), .out(OUT_M), .sel(multiplexer_1_out));
endmodule

module TIMER (
  input  [15:0] MASK,
  input  [15:0] PRESCALER,
  input  [15:0] CNT_IN,
  input  CNT_CHANGED,
  input  CLK,
  output INTERRUPT,
  output [15:0] COUNTER_VAL,
  output PRE_INTERRUPT
);

  wire and_1_out, comparator_1_lt, counter_2_carry, not_1_out, or_1_out;
  wire [1:0] bit_extender_1_out;
  wire [15:0] counter_1_q;

  Bit_Extender #(.in_width(16), .out_width(2)) bit_extender_1 (.in(MASK), .out(bit_extender_1_out));
  Counter #(.max('hffff), .width(16)) counter_1 (
    .clr(not_1_out), .count(bit_extender_1_out[1]), .clk(CLK), .Q(counter_1_q));  // open: load, up, D, carry
  Comparator #(.width(16)) comparator_1 (.a(counter_1_q), .b(PRESCALER), .lt(comparator_1_lt));  // open: gt, eq
  not not_1 (not_1_out, comparator_1_lt);
  and and_1 (and_1_out, CNT_CHANGED, CLK);
  Counter #(.max('h100), .width(16)) counter_2 (
    .clr(counter_2_carry), .load(CNT_CHANGED), .clk(or_1_out), .D(CNT_IN), .carry(counter_2_carry),
    .Q(COUNTER_VAL));  // open: up, count
  or or_1 (or_1_out, not_1_out, and_1_out);
  and and_2 (INTERRUPT, bit_extender_1_out[0], counter_2_carry);
  Comparator #(.width(16)) comparator_2 (.a(COUNTER_VAL), .b(16'hff), .eq(PRE_INTERRUPT));  // open: gt, lt
endmodule

module SCREEN_DRIVER (
  input  [15:0] SCREEN_INSTRUCTION,
  output [23:0] RGB_COLOR,
  output [4:0] Y,
  output [4:0] X
);

  wire [7:0] color_converter_1_out_2, color_converter_2_out_2, color_converter_3_out_2;
  wire [23:0] adder_1_out, bit_extender_1_out, bit_extender_2_out, bit_extender_3_out, shifter_1_out,
       shifter_2_out;

  COLOR_CONVERTER color_converter_1 (.out_2(color_converter_1_out_2), .in_1(SCREEN_INSTRUCTION[1:0]));
  COLOR_CONVERTER color_converter_2 (.out_2(color_converter_2_out_2), .in_1(SCREEN_INSTRUCTION[3:2]));
  COLOR_CONVERTER color_converter_3 (.out_2(color_converter_3_out_2), .in_1(SCREEN_INSTRUCTION[5:4]));
  assign bit_extender_1_out = {{16{1'b0}}, color_converter_1_out_2};  // Bit_Extender bit_extender_1
  assign bit_extender_2_out = {{16{1'b0}}, color_converter_2_out_2};  // Bit_Extender bit_extender_2
  assign bit_extender_3_out = {{16{1'b0}}, color_converter_3_out_2};  // Bit_Extender bit_extender_3
  Adder #(.width(24)) adder_1 (.a(bit_extender_1_out), .b(shifter_1_out), .out(adder_1_out));  // open: cin, cout
  Shifter #(.width(24)) shifter_1 (.in(bit_extender_2_out), .\dist (5'b01000), .out(shifter_1_out));
  Shifter #(.width(24)) shifter_2 (.in(bit_extender_3_out), .\dist (5'b10000), .out(shifter_2_out));
  Adder #(.width(24)) adder_2 (.a(adder_1_out), .b(shifter_2_out), .out(RGB_COLOR));  // open: cin, cout

  assign X = SCREEN_INSTRUCTION[15:11];
  assign Y = SCREEN_INSTRUCTION[10:6];

  // Notes on the sheet:
  //   B
  //   G
  //   R
  //   Y
  //   X
endmodule

module COLOR_CONVERTER (
  input  [1:0] in_1,
  output [7:0] out_2
);

  Multiplexer #(.enable("false"), .select(2), .width(8)) multiplexer_1 (
    .in0({8{1'b0}}), .in1(8'h55), .in2(8'haa), .in3({8{1'b1}}), .out(out_2), .sel(in_1));
endmodule
