// Logisim project CPUcustom.circ as structural Verilog: 23 circuits, main circuit main
module main (
  input  CLK,
  input  RST,
  input  [15:0] INP,
  input  [6:0] KBRD,
  output [15:0] OUTP
);

  wire counter_timer_1_flag, counter_timer_1_overflow, cpu_1_stack_enable, cpu_1_write_in_memory,
       memories_1_counter_changed, or_1_out;
  wire [14:0] cpu_1_adress_memory, cpu_1_pc_outp, cpu_1_stack_point;
  wire [15:0] bit_extender_1_out, counter_timer_1_coutner_outp, cpu_1_outp, cpu_1_stack_outp,
       memories_1_counter, memories_1_ddr_outp, memories_1_mask, memories_1_memory_out, memories_1_port_outp,
       memories_1_presc, memories_1_stack_out, port_controller_1_pin_outp, rom_1_data;

  ROM #(.addrWidth(15), .dataWidth(16)) rom_1 (.addr(cpu_1_pc_outp), .data(rom_1_data));
  LED led_1 (.in(CLK));
  CPU cpu_1 (
    .Write_in_memory(cpu_1_write_in_memory), .Adress_memory(cpu_1_adress_memory), .PC_Outp(cpu_1_pc_outp),
    .OUTP(cpu_1_outp), .Stack_OUTP(cpu_1_stack_outp), .Stack_enable(cpu_1_stack_enable),
    .Stack_point(cpu_1_stack_point), .FLAG(counter_timer_1_flag), .Stack_out(memories_1_stack_out),
    .Instruction(rom_1_data), .CLK(CLK), .INTERRUPT(counter_timer_1_overflow),
    .Memory(memories_1_memory_out), .Reset(RST));
  or or_1 (or_1_out, CLK, counter_timer_1_overflow);
  Memories memories_1 (
    .DDR_OUTP(memories_1_ddr_outp), .PORT_OUTP(memories_1_port_outp), .stack_out(memories_1_stack_out),
    .Counter_Changed(memories_1_counter_changed), .MASK(memories_1_mask), .PRESC(memories_1_presc),
    .COUNTER(memories_1_counter), .memory_out(memories_1_memory_out),
    .Counter_INP(counter_timer_1_coutner_outp), .PIN_INP(port_controller_1_pin_outp),
    .KBRD(bit_extender_1_out), .Stack_pointer(cpu_1_stack_point), .Stack_operation(cpu_1_stack_enable),
    .Push_in_stack(cpu_1_stack_outp), .Adress_in_memory(cpu_1_adress_memory),
    .Write_in_M_enable(cpu_1_write_in_memory), .CLK(or_1_out), .Write_in_M_val(cpu_1_outp));  // open: out_15
  Port_Controller port_controller_1 (
    .OUTP(OUTP), .PIN_OUTP(port_controller_1_pin_outp), .INP(INP), .DDR_INP(memories_1_ddr_outp),
    .PORT_INP(memories_1_port_outp));
  assign bit_extender_1_out = {{9{1'b0}}, KBRD};  // Bit_Extender bit_extender_1
  Counter_Timer counter_timer_1 (
    .Coutner_OUTP(counter_timer_1_coutner_outp), .OVERFLOW(counter_timer_1_overflow),
    .FLAG(counter_timer_1_flag), .MASK(memories_1_mask), .PRESCALER(memories_1_presc), .CLK(CLK),
    .COUNTER_INP(memories_1_counter), .LOAD(memories_1_counter_changed));
  LED led_2 (.in(OUTP[12]));
  LED led_3 (.in(OUTP[13]));
  LED led_4 (.in(OUTP[14]));
  LED led_5 (.in(OUTP[15]));
  LED led_6 (.in(OUTP[8]));
  LED led_7 (.in(OUTP[9]));
  LED led_8 (.in(OUTP[10]));
  LED led_9 (.in(OUTP[11]));
  LED led_10 (.in(OUTP[7]));
  LED led_11 (.in(OUTP[6]));
  LED led_12 (.in(OUTP[5]));
  LED led_13 (.in(OUTP[4]));
  LED led_14 (.in(OUTP[3]));
  LED led_15 (.in(OUTP[2]));
  LED led_16 (.in(OUTP[1]));
  LED led_17 (.in(OUTP[0]));

  // Notes on the sheet:
  //   contents of rom_1 (hex, n*v repeats v):
  //   3 8090 4 8150 7 8390 6 8007
endmodule

module CPU (
  input  [15:0] Instruction,
  input  [15:0] Memory,
  input  [15:0] Stack_out,
  input  Reset,
  input  CLK,
  input  INTERRUPT,
  input  FLAG,
  output [15:0] OUTP,
  output [15:0] Stack_OUTP,
  output Write_in_memory,
  output [14:0] Adress_memory,
  output [14:0] PC_Outp,
  output Stack_enable,
  output [14:0] Stack_point
);

  wire a_or_m_1_a, and_2_out, and_3_out, and_4_out, and_5_out, and_6_out, and_8_out, det_dest_1_a,
       det_dest_1_d, det_dest_1_m, det_dest_1_push_pop, det_dest_1_s, det_instr_1_a, det_instr_1_c,
       jumt_or_not_to_jump_1_jump, not_2_out, not_3_out, not_4_out, or_1_out, or_2_out, or_3_out;
  wire [0:0] and_9_out;
  wire [2:0] jmp_bits_1_out_2, operand_operator_1_operand, operand_operator_1_operator;
  wire [14:0] stack_counter_1_stack_pointer;
  wire [15:0] and_1_out, D_q, multiplexer_1_out, multiplexer_2_out, multiplexer_3_out, multiplexer_4_out,
       operand_operator_selector_1_inp1, operand_operator_selector_1_inp2;
  wire [15:15] A_q, not_1_out, pc_1_outp;

  not not_1 (not_1_out[15], FLAG);
  assign and_1_out = Instruction & {16{not_1_out[15]}};  // AND_Gate and_1, 16 bits wide
  DET_DEST det_dest_1 (
    .D(det_dest_1_d), .M(det_dest_1_m), .A(det_dest_1_a), .S(det_dest_1_s), .Push_Pop(det_dest_1_push_pop),
    .Instruction(and_1_out));
  DET_INSTR det_instr_1 (.A(det_instr_1_a), .C(det_instr_1_c), .in_1(and_1_out));
  A_OR_M a_or_m_1 (.A(a_or_m_1_a), .in_1(and_1_out));
  jmp_bits jmp_bits_1 (.out_2(jmp_bits_1_out_2), .in_1(and_1_out));
  Multiplexer #(.enable("false"), .width(16)) multiplexer_1 (
    .in0(and_1_out), .in1(OUTP), .out(multiplexer_1_out), .sel(not_2_out));
  not not_2 (not_2_out, det_instr_1_a);
  OPERAND_OPERATOR operand_operator_1 (
    .OPERAND(operand_operator_1_operand), .OPERATOR(operand_operator_1_operator), .in_1(and_1_out));
  and and_2 (and_2_out, det_instr_1_c, det_dest_1_a);
  Multiplexer #(.enable("false"), .width(16)) multiplexer_2 (
    .in0({A_q[15], Adress_memory}), .in1(OUTP), .out(multiplexer_2_out), .sel(det_dest_1_a));
  or or_1 (or_1_out, and_2_out, det_instr_1_a);
  not not_3 (not_3_out, FLAG);
  Register #(.width(16)) A (
    .D(multiplexer_1_out), .en(and_3_out), .clk(CLK), .Q({A_q[15], Adress_memory}), .clr(Reset));
  and and_3 (and_3_out, or_1_out, not_3_out);
  Register #(.width(16)) D (.D(OUTP), .en(and_4_out), .clk(CLK), .Q(D_q), .clr(Reset));
  and and_4 (and_4_out, det_dest_1_d, det_instr_1_c);
  jumt_or_not_to_jump jumt_or_not_to_jump_1 (
    .jump(jumt_or_not_to_jump_1_jump), .C(det_instr_1_c), .jmp_bits(jmp_bits_1_out_2), .alu_OUTP(OUTP));
  and and_5 (and_5_out, det_instr_1_c, det_dest_1_s);
  Multiplexer #(.enable("false"), .width(16)) multiplexer_3 (
    .in0({A_q[15], Adress_memory}), .in1(Memory), .out(multiplexer_3_out), .sel(a_or_m_1_a));
  or or_2 (or_2_out, Reset, INTERRUPT);
  or or_3 (or_3_out, and_5_out, FLAG);
  Multiplexer #(.enable("false"), .width(16)) multiplexer_4 (
    .in0(multiplexer_3_out), .in1(Stack_out), .out(multiplexer_4_out), .sel(and_6_out));
  and and_6 (and_6_out, det_dest_1_s, det_dest_1_push_pop);
  PC pc_1 (
    .OUTP({pc_1_outp[15], PC_Outp}), .LOAD(jumt_or_not_to_jump_1_jump), .RESET(or_2_out),
    .INP(multiplexer_2_out), .CLCK(CLK));
  stack_counter stack_counter_1 (
    .RESET(Reset), .CLK(CLK), .PUSH(det_dest_1_push_pop), .enable(or_3_out),
    .Stack_pointer(stack_counter_1_stack_pointer));
  Operand_Operator_Selector operand_operator_selector_1 (
    .D(D_q), .A(multiplexer_4_out), .Operand(operand_operator_1_operand),
    .INP1(operand_operator_selector_1_inp1), .INP2(operand_operator_selector_1_inp2));
  and and_7 (Write_in_memory, det_instr_1_c, det_dest_1_m);
  ALU alu_1 (
    .out_4(OUTP), .INP1(operand_operator_selector_1_inp1), .INP2(operand_operator_selector_1_inp2),
    .SEL(operand_operator_1_operator));
  not not_4 (not_4_out, det_dest_1_push_pop);
  and and_8 (and_8_out, det_instr_1_c, not_4_out, det_dest_1_s);
  or or_4 (Stack_enable, and_8_out, INTERRUPT, FLAG);
  and and_9 (and_9_out[0], det_instr_1_c, det_dest_1_push_pop, det_dest_1_s);
  Subtractor #(.width(15)) subtractor_1 (
    .a(stack_counter_1_stack_pointer), .b({{14{1'b0}}, and_9_out[0]}), .out(Stack_point));  // open: bin, bout
  Multiplexer #(.enable("false"), .width(16)) multiplexer_5 (
    .in0(OUTP), .in1({pc_1_outp[15], PC_Outp}), .out(Stack_OUTP), .sel(FLAG));
endmodule

module ALU (
  input  [15:0] INP1,
  input  [15:0] INP2,
  input  [2:0] SEL,
  output [15:0] out_4
);

  wire [15:0] adder_1_out, and_1_out, divider_1_out, multiplier_1_out, not_1_out, or_1_out, subtractor_1_out,
       xor_1_out;

  Adder #(.width(16)) adder_1 (.a(INP1), .b(INP2), .out(adder_1_out));  // open: cin, cout
  Subtractor #(.width(16)) subtractor_1 (.a(INP1), .b(INP2), .out(subtractor_1_out));  // open: bin, bout
  Multiplier #(.width(16)) multiplier_1 (.a(INP1), .b(INP2), .out(multiplier_1_out));  // open: cin, cout
  Divider #(.width(16)) divider_1 (.a(INP1), .b(INP2), .out(divider_1_out));  // open: upper, rem
  assign not_1_out = ~INP2;  // NOT_Gate not_1, 16 bits wide
  assign and_1_out = INP1 & INP2;  // AND_Gate and_1, 16 bits wide
  assign or_1_out = INP1 | INP2;  // OR_Gate or_1, 16 bits wide
  assign xor_1_out = INP1 ^ INP2;  // XOR_Gate xor_1, 16 bits wide
  Multiplexer #(.enable("false"), .select(3), .width(16)) multiplexer_1 (
    .in0(adder_1_out), .in1(subtractor_1_out), .in2(multiplier_1_out), .in3(divider_1_out), .in4(not_1_out),
    .in5(and_1_out), .in6(or_1_out), .in7(xor_1_out), .out(out_4), .sel(SEL));
endmodule

module PC (
  input  LOAD,
  input  [15:0] INP,
  input  CLCK,
  input  RESET,
  output [15:0] OUTP
);

  Counter #(.max('hffff), .width(16)) PC_COUNT (
    .load(LOAD), .D(INP), .Q(OUTP), .clk(CLCK), .clr(RESET));  // open: count, carry, up
endmodule

module Operand_Operator_Selector (
  input  [15:0] D,
  input  [15:0] A,
  input  [2:0] Operand,
  output [15:0] INP1,
  output [15:0] INP2
);

  Multiplexer #(.enable("false"), .select(3), .width(16)) multiplexer_1 (
    .in0({16{1'b0}}), .in1(D), .in2({16{1'b0}}), .in3({16{1'b0}}), .in4(A), .in5({16{1'b0}}), .in6(A),
    .in7(D), .out(INP1), .sel(Operand));
  Multiplexer #(.enable("false"), .select(3), .width(16)) multiplexer_2 (
    .in0({16{1'b0}}), .in1(A), .in2(A), .in3(D), .in4(D), .in5(16'h1), .in6(16'h1), .in7(16'h1), .out(INP2),
    .sel(Operand));
endmodule

module DET_INSTR (
  input  [15:0] in_1,
  output A,
  output C
);

  IS_A_INST is_a_inst_1 (.out_2(A), .in_1(in_1));
  IS_C_INST is_c_inst_1 (.C(C), .in_1(in_1));
endmodule

module IS_A_INST (
  input  [15:0] in_1,
  output out_2
);

  not not_1 (out_2, in_1[15]);
endmodule

module IS_C_INST (
  input  [15:0] in_1,
  output C
);


  assign C = in_1[15];
endmodule

module DET_DEST (
  input  [15:0] Instruction,
  output D,
  output M,
  output A,
  output S,
  output Push_Pop
);


  assign A = Instruction[5];
  assign D = Instruction[3];
  assign M = Instruction[4];
  assign Push_Pop = Instruction[13];
  assign S = Instruction[14];
endmodule

module A_OR_M (
  input  [15:0] in_1,
  output A
);


  assign A = in_1[9];
endmodule

module OPERAND_OPERATOR (
  input  [15:0] in_1,
  output [2:0] OPERAND,
  output [2:0] OPERATOR
);


  assign OPERAND = in_1[8:6];
  assign OPERATOR = in_1[12:10];
endmodule

module jmp_bits (
  input  [15:0] in_1,
  output [2:0] out_2
);


  assign out_2 = in_1[2:0];
endmodule

module jumt_or_not_to_jump (
  input  [2:0] jmp_bits,
  input  [15:0] alu_OUTP,
  input  C,
  output jump
);

  wire and_1_out, and_2_out, and_3_out, comparator_1_eq, comparator_1_gt, comparator_1_lt, or_1_out;

  Comparator #(.width(16)) comparator_1 (
    .a(alu_OUTP), .b({16{1'b0}}), .gt(comparator_1_gt), .eq(comparator_1_eq), .lt(comparator_1_lt));
  and and_1 (and_1_out, jmp_bits[0], comparator_1_gt);
  and and_2 (and_2_out, comparator_1_eq, jmp_bits[1]);
  and and_3 (and_3_out, comparator_1_lt, jmp_bits[2]);
  or or_1 (or_1_out, and_1_out, and_2_out, and_3_out);
  and and_4 (jump, or_1_out, C);
endmodule

module Delay (
  input  in_1,
  output out_2
);

  wire not_1_out, not_2_out, not_3_out, not_4_out, not_5_out, not_6_out, not_7_out, not_8_out, not_9_out,
       not_10_out, not_11_out, not_12_out, not_13_out, not_14_out, not_15_out, not_16_out, not_17_out,
       not_18_out, not_19_out, not_20_out, not_21_out, not_22_out, not_23_out, not_24_out, not_25_out,
       not_26_out, not_27_out, not_28_out, not_29_out, not_30_out, not_31_out, not_32_out, not_33_out,
       not_34_out, not_35_out, not_36_out, not_37_out, not_38_out, not_39_out, not_40_out, not_41_out,
       not_42_out, not_43_out, not_44_out, not_45_out, not_46_out, not_47_out, not_48_out, not_49_out,
       not_50_out, not_51_out, not_52_out, not_53_out, not_54_out, not_55_out, not_56_out, not_57_out,
       not_58_out, not_59_out, not_60_out, not_61_out, not_62_out, not_63_out;

  not not_1 (not_1_out, in_1);
  not not_2 (not_2_out, not_1_out);
  not not_3 (not_3_out, not_2_out);
  not not_4 (not_4_out, not_56_out);
  not not_5 (not_5_out, not_4_out);
  not not_6 (not_6_out, not_5_out);
  not not_7 (not_7_out, not_58_out);
  not not_8 (not_8_out, not_7_out);
  not not_9 (not_9_out, not_8_out);
  not not_10 (not_10_out, not_61_out);
  not not_11 (not_11_out, not_10_out);
  not not_12 (not_12_out, not_11_out);
  not not_13 (not_13_out, not_3_out);
  not not_14 (not_14_out, not_13_out);
  not not_15 (not_15_out, not_14_out);
  not not_16 (not_16_out, not_6_out);
  not not_17 (not_17_out, not_16_out);
  not not_18 (not_18_out, not_17_out);
  not not_19 (not_19_out, not_9_out);
  not not_20 (not_20_out, not_19_out);
  not not_21 (not_21_out, not_12_out);
  not not_22 (not_22_out, not_21_out);
  not not_23 (not_23_out, not_15_out);
  not not_24 (not_24_out, not_23_out);
  not not_25 (not_25_out, not_18_out);
  not not_26 (not_26_out, not_25_out);
  not not_27 (not_27_out, not_20_out);
  not not_28 (not_28_out, not_27_out);
  not not_29 (not_29_out, not_28_out);
  not not_30 (not_30_out, not_22_out);
  not not_31 (not_31_out, not_30_out);
  not not_32 (not_32_out, not_31_out);
  not not_33 (not_33_out, not_24_out);
  not not_34 (not_34_out, not_33_out);
  not not_35 (not_35_out, not_34_out);
  not not_36 (not_36_out, not_26_out);
  not not_37 (not_37_out, not_36_out);
  not not_38 (not_38_out, not_37_out);
  not not_39 (not_39_out, not_29_out);
  not not_40 (not_40_out, not_39_out);
  not not_41 (not_41_out, not_40_out);
  not not_42 (not_42_out, not_32_out);
  not not_43 (not_43_out, not_42_out);
  not not_44 (not_44_out, not_43_out);
  not not_45 (not_45_out, not_35_out);
  not not_46 (not_46_out, not_45_out);
  not not_47 (not_47_out, not_46_out);
  not not_48 (not_48_out, not_38_out);
  not not_49 (not_49_out, not_48_out);
  not not_50 (not_50_out, not_49_out);
  not not_51 (not_51_out, not_41_out);
  not not_52 (not_52_out, not_51_out);
  not not_53 (not_53_out, not_44_out);
  not not_54 (not_54_out, not_53_out);
  not not_55 (not_55_out, not_47_out);
  not not_56 (not_56_out, not_55_out);
  not not_57 (not_57_out, not_50_out);
  not not_58 (not_58_out, not_57_out);
  not not_59 (not_59_out, not_52_out);
  not not_60 (not_60_out, not_59_out);
  not not_61 (not_61_out, not_60_out);
  not not_62 (not_62_out, not_54_out);
  not not_63 (not_63_out, not_62_out);
  not not_64 (out_2, not_63_out);
endmodule

module double_edged (
  input  CLK,
  input  D,
  output out_3
);

  wire d_ff_1_q, d_ff_2_q, not_1_out;

  not not_1 (not_1_out, CLK);
  D_Flip_Flop d_ff_1 (.D(D), .clk(CLK), .Q(d_ff_1_q), .reset(out_3));  // open: Qn, preset
  D_Flip_Flop d_ff_2 (.D(D), .clk(not_1_out), .Q(d_ff_2_q), .preset(out_3), .reset(out_3));  // open: Qn
  Multiplexer #(.enable("false")) multiplexer_1 (.in0(d_ff_2_q), .in1(d_ff_1_q), .out(out_3), .sel(CLK));
endmodule

module stack_counter (
  input  RESET,
  input  CLK,
  input  PUSH,
  input  enable,
  output [14:0] Stack_pointer
);

  wire not_1_out;

  Counter #(.max('h7fff), .width(15)) Stack_Count (
    .clr(RESET), .up(not_1_out), .count(enable), .clk(CLK), .Q(Stack_pointer));  // open: load, D, carry
  not not_1 (not_1_out, PUSH);
endmodule

module Memories (
  input  [14:0] Adress_in_memory,
  input  Write_in_M_enable,
  input  CLK,
  input  [15:0] Write_in_M_val,
  input  [14:0] Stack_pointer,
  input  Stack_operation,
  input  [15:0] PIN_INP,
  input  [15:0] Push_in_stack,
  input  [15:0] Counter_INP,
  input  [15:0] KBRD,
  output [15:0] DDR_OUTP,
  output [15:0] PORT_OUTP,
  output [15:0] memory_out,
  output Counter_Changed,
  output [15:0] out_15,
  output [15:0] stack_out,
  output [15:0] MASK,
  output [15:0] PRESC,
  output [15:0] COUNTER
);

  wire memory_controller_1_ddr_write, memory_controller_1_keyboard, memory_controller_1_mask,
       memory_controller_1_port_write, memory_controller_1_prescaler, memory_controller_1_write_ram;
  wire [14:0] memory_controller_1_ram_address;
  wire [15:0] COUNTER_REG_q, KEYBOAD_q, PIN_REGIS_pin_outp, ram_1_dout;

  Memory_Controller memory_controller_1 (
    .PORT_WRITE(memory_controller_1_port_write), .RAM_ADDRESS(memory_controller_1_ram_address),
    .WRITE_RAM(memory_controller_1_write_ram), .DDR_WRITE(memory_controller_1_ddr_write),
    .MASK(memory_controller_1_mask), .PRESCALER(memory_controller_1_prescaler), .COUNTER(Counter_Changed),
    .KEYBOARD(memory_controller_1_keyboard), .WRITE_M(Write_in_M_enable), .ADRESS(Adress_in_memory));  // open: PIN_WRITE
  Multiplexer #(.enable("false"), .width(16)) multiplexer_1 (
    .in0(Counter_INP), .in1(Write_in_M_val), .out(COUNTER), .sel(Counter_Changed));
  RAM #(.addrWidth(15), .dataWidth(16), .enables("line")) ram_1 (
    .addr(memory_controller_1_ram_address), .we(memory_controller_1_write_ram), .clk(CLK),
    .din(Write_in_M_val), .dout(ram_1_dout));
  RAM #(.addrWidth(15), .dataWidth(16), .enables("line")) Stack_Memory (
    .addr(Stack_pointer), .we(Stack_operation), .clk(CLK), .din(Push_in_stack), .dout(stack_out));
  Register #(.width(16)) DDR_REG (
    .D(Write_in_M_val), .en(memory_controller_1_ddr_write), .clk(CLK), .Q(DDR_OUTP));  // open: clr
  Register #(.width(16)) PORT_REG (
    .D(Write_in_M_val), .en(memory_controller_1_port_write), .clk(CLK), .Q(PORT_OUTP));  // open: clr
  Register #(.width(16)) MASK_REG (
    .D(Write_in_M_val), .en(memory_controller_1_mask), .clk(CLK), .Q(MASK));  // open: clr
  Register #(.width(16)) PRESCALER_REG (
    .D(Write_in_M_val), .en(memory_controller_1_prescaler), .clk(CLK), .Q(PRESC));  // open: clr
  Register #(.width(16)) COUNTER_REG (.D(COUNTER), .en(CLK), .clk(CLK), .Q(COUNTER_REG_q));  // open: clr
  Register #(.width(16)) KEYBOAD (.D(KBRD), .en(CLK), .clk(CLK), .Q(KEYBOAD_q));  // open: clr
  PIN_REG PIN_REGIS (.PIN_OUTP(PIN_REGIS_pin_outp), .PIN_INP(PIN_INP));
  Memory_read memory_read_1 (
    .OUTP(memory_out), .ADDR(Adress_in_memory), .KEYBOARD(KEYBOAD_q), .MASK(MASK), .PRESCALER(PRESC),
    .COUNTER(COUNTER_REG_q), .PORT_VAL(PORT_OUTP), .PIN_VAL(PIN_REGIS_pin_outp), .RAM_VAL(ram_1_dout),
    .DDR_VAL(DDR_OUTP));
endmodule

module Port_Controller (
  input  [15:0] INP,
  input  [15:0] DDR_INP,
  input  [15:0] PORT_INP,
  output [15:0] OUTP,
  output [15:0] PIN_OUTP
);

  wire [15:0] not_1_out;

  assign not_1_out = ~DDR_INP;  // NOT_Gate not_1, 16 bits wide
  assign PIN_OUTP = not_1_out & INP;  // AND_Gate and_1, 16 bits wide
  assign OUTP = DDR_INP & PORT_INP;  // AND_Gate and_2, 16 bits wide
endmodule

module Counter_Timer (
  input  LOAD,
  input  [15:0] COUNTER_INP,
  input  [15:0] PRESCALER,
  input  CLK,
  input  [15:0] MASK,
  output OVERFLOW,
  output [15:0] Coutner_OUTP,
  output FLAG
);

  wire and_1_out, comparator_1_eq, comparator_1_gt, comparator_2_eq, comparator_2_gt, or_1_out, or_2_out,
       or_3_out;
  wire [15:0] Clock_Counter_q;

  Counter #(.max('hffff), .width(16)) Clock_Counter (
    .clr(or_1_out), .count(MASK[1]), .clk(CLK), .Q(Clock_Counter_q));  // open: load, up, D, carry
  Comparator #(.width(16)) comparator_1 (
    .a(Clock_Counter_q), .b(PRESCALER), .gt(comparator_1_gt), .eq(comparator_1_eq));  // open: lt
  or or_1 (or_1_out, comparator_1_gt, comparator_1_eq);
  and and_1 (and_1_out, LOAD, CLK);
  or or_2 (or_2_out, or_1_out, and_1_out);
  Counter #(.max('hffff), .width(16)) counter_1 (
    .clr(or_3_out), .load(LOAD), .clk(or_2_out), .D(COUNTER_INP), .Q(Coutner_OUTP));  // open: up, count, carry
  or or_3 (or_3_out, comparator_2_gt, comparator_2_eq);
  Comparator #(.width(16)) comparator_2 (
    .a(Coutner_OUTP), .b(16'h100), .gt(comparator_2_gt), .eq(comparator_2_eq));  // open: lt
  and and_2 (OVERFLOW, or_3_out, MASK[0]);
  Comparator #(.width(16)) comparator_3 (.a(Coutner_OUTP), .b(16'hff), .eq(FLAG));  // open: gt, lt

  // Notes on the sheet:
  //   ON_OFF
  //   OF_INTERRUPT
endmodule

module Memory_Controller (
  input  WRITE_M,
  input  [14:0] ADRESS,
  output DDR_WRITE,
  output PORT_WRITE,
  output PIN_WRITE,
  output [14:0] RAM_ADDRESS,
  output WRITE_RAM,
  output MASK,
  output PRESCALER,
  output COUNTER,
  output KEYBOARD
);

  wire comparator_1_eq, comparator_2_eq, comparator_3_eq, comparator_4_eq, comparator_4_gt, comparator_5_eq,
       comparator_6_eq, comparator_7_eq, comparator_8_eq, or_1_out;

  Subtractor #(.width(15)) subtractor_1 (.a(ADRESS), .b(15'h7), .out(RAM_ADDRESS));  // open: bin, bout
  Comparator #(.width(15)) comparator_1 (.a(ADRESS), .b({15{1'b0}}), .eq(comparator_1_eq));  // open: gt, lt
  Comparator #(.width(15)) comparator_2 (.a(ADRESS), .b(15'h1), .eq(comparator_2_eq));  // open: gt, lt
  Comparator #(.width(15)) comparator_3 (.a(ADRESS), .b(15'h2), .eq(comparator_3_eq));  // open: gt, lt
  Comparator #(.width(15)) comparator_4 (
    .a(ADRESS), .b(15'h7), .gt(comparator_4_gt), .eq(comparator_4_eq));  // open: lt
  Comparator #(.width(15)) comparator_5 (.a(ADRESS), .b(15'h3), .eq(comparator_5_eq));  // open: gt, lt
  Comparator #(.width(15)) comparator_6 (.a(ADRESS), .b(15'h4), .eq(comparator_6_eq));  // open: gt, lt
  Comparator #(.width(15)) comparator_7 (.a(ADRESS), .b(15'h5), .eq(comparator_7_eq));  // open: gt, lt
  Comparator #(.width(15)) comparator_8 (.a(ADRESS), .b(15'h6), .eq(comparator_8_eq));  // open: gt, lt
  and and_1 (DDR_WRITE, WRITE_M, comparator_1_eq);
  and and_2 (PORT_WRITE, WRITE_M, comparator_2_eq);
  and and_3 (PIN_WRITE, WRITE_M, comparator_3_eq);
  or or_1 (or_1_out, comparator_4_gt, comparator_4_eq);
  and and_4 (WRITE_RAM, or_1_out, WRITE_M);
  and and_5 (MASK, WRITE_M, comparator_5_eq);
  and and_6 (PRESCALER, WRITE_M, comparator_6_eq);
  and and_7 (COUNTER, WRITE_M, comparator_7_eq);
  and and_8 (KEYBOARD, WRITE_M, comparator_8_eq);
endmodule

module Memory_read (
  input  [15:0] DDR_VAL,
  input  [15:0] PORT_VAL,
  input  [15:0] PIN_VAL,
  input  [15:0] RAM_VAL,
  input  [14:0] ADDR,
  input  [15:0] MASK,
  input  [15:0] PRESCALER,
  input  [15:0] COUNTER,
  input  [15:0] KEYBOARD,
  output [15:0] OUTP
);

  wire comparator_1_eq, comparator_2_eq, comparator_3_eq, comparator_4_eq, comparator_5_eq, comparator_6_eq,
       comparator_7_eq, comparator_8_eq, comparator_8_gt, or_1_out;
  wire [15:0] and_1_out, and_2_out, and_3_out, and_4_out, and_5_out, and_6_out, and_7_out, and_8_out,
       bit_extender_1_out, bit_extender_2_out, bit_extender_3_out, bit_extender_4_out, bit_extender_5_out,
       bit_extender_6_out, bit_extender_7_out, bit_extender_8_out;

  Comparator #(.width(15)) comparator_1 (.a(ADDR), .b({15{1'b0}}), .eq(comparator_1_eq));  // open: gt, lt
  Comparator #(.width(15)) comparator_2 (.a(ADDR), .b(15'h1), .eq(comparator_2_eq));  // open: gt, lt
  Comparator #(.width(15)) comparator_3 (.a(ADDR), .b(15'h2), .eq(comparator_3_eq));  // open: gt, lt
  Comparator #(.width(15)) comparator_4 (.a(ADDR), .b(15'h3), .eq(comparator_4_eq));  // open: gt, lt
  Comparator #(.width(15)) comparator_5 (.a(ADDR), .b(15'h4), .eq(comparator_5_eq));  // open: gt, lt
  Comparator #(.width(15)) comparator_6 (.a(ADDR), .b(15'h5), .eq(comparator_6_eq));  // open: gt, lt
  Comparator #(.width(15)) comparator_7 (.a(ADDR), .b(15'h6), .eq(comparator_7_eq));  // open: gt, lt
  Comparator #(.width(15)) comparator_8 (.a(ADDR), .b(15'h7), .gt(comparator_8_gt), .eq(comparator_8_eq));  // open: lt
  or or_1 (or_1_out, comparator_8_gt, comparator_8_eq);
  assign bit_extender_1_out = {{15{comparator_1_eq}}, comparator_1_eq};  // Bit_Extender bit_extender_1
  assign bit_extender_2_out = {{15{comparator_2_eq}}, comparator_2_eq};  // Bit_Extender bit_extender_2
  assign bit_extender_3_out = {{15{comparator_3_eq}}, comparator_3_eq};  // Bit_Extender bit_extender_3
  assign bit_extender_4_out = {{15{comparator_4_eq}}, comparator_4_eq};  // Bit_Extender bit_extender_4
  assign bit_extender_5_out = {{15{comparator_5_eq}}, comparator_5_eq};  // Bit_Extender bit_extender_5
  assign bit_extender_6_out = {{15{comparator_6_eq}}, comparator_6_eq};  // Bit_Extender bit_extender_6
  assign bit_extender_7_out = {{15{comparator_7_eq}}, comparator_7_eq};  // Bit_Extender bit_extender_7
  assign bit_extender_8_out = {{15{or_1_out}}, or_1_out};  // Bit_Extender bit_extender_8
  assign and_1_out = DDR_VAL & bit_extender_1_out;  // AND_Gate and_1, 16 bits wide
  assign and_2_out = PORT_VAL & bit_extender_2_out;  // AND_Gate and_2, 16 bits wide
  assign and_3_out = PIN_VAL & bit_extender_3_out;  // AND_Gate and_3, 16 bits wide
  assign and_4_out = RAM_VAL & bit_extender_8_out;  // AND_Gate and_4, 16 bits wide
  assign and_5_out = bit_extender_4_out & MASK;  // AND_Gate and_5, 16 bits wide
  assign and_6_out = bit_extender_5_out & PRESCALER;  // AND_Gate and_6, 16 bits wide
  assign and_7_out = bit_extender_6_out & COUNTER;  // AND_Gate and_7, 16 bits wide
  assign and_8_out = bit_extender_7_out & KEYBOARD;  // AND_Gate and_8, 16 bits wide
  assign OUTP = and_1_out | and_2_out | and_3_out | and_4_out | and_5_out | and_6_out | and_7_out | and_8_out;  // OR_Gate or_2, 16 bits wide
endmodule

module PIN_REG (
  input  [15:0] PIN_INP,
  output [15:0] PIN_OUTP
);

  wire comparator_1_eq, not_1_out, or_1_out;

  Comparator #(.width(16)) comparator_1 (.a(PIN_INP), .b(PIN_OUTP), .eq(comparator_1_eq));  // open: gt, lt
  Register #(.width(16)) register_1 (.D(PIN_INP), .en(or_1_out), .clk(or_1_out), .Q(PIN_OUTP));  // open: clr
  buf or_1 (or_1_out, not_1_out);  // OR_Gate
  not not_1 (not_1_out, comparator_1_eq);
endmodule

module test (
  input  in_1,
  input  [15:0] in_2,
  input  in_3
);

  wire clock_1_out;
  wire [6:0] keyboard_1_data;
  wire [15:0] main_1_outp;

  Keyboard keyboard_1 (.clk(clock_1_out), .re(clock_1_out), .clr(in_3), .data(keyboard_1_data));  // open: avail
  Clock clock_1 (.out(clock_1_out));
  TTY tty_1 ();  // open: data, clk, we, clr
  main main_1 (.OUTP(main_1_outp), .KBRD(keyboard_1_data), .INP(in_2), .CLK(clock_1_out), .RST(in_1));
  LED led_1 (.in(main_1_outp[0]));
  LED led_2 (.in(main_1_outp[1]));
  LED led_3 (.in(main_1_outp[2]));
  LED led_4 (.in(main_1_outp[3]));
  LED led_5 (.in(main_1_outp[4]));
  LED led_6 (.in(main_1_outp[5]));
  LED led_7 (.in(main_1_outp[6]));
  LED led_8 (.in(main_1_outp[7]));
  LED led_9 (.in(main_1_outp[8]));
  LED led_10 (.in(main_1_outp[9]));
  LED led_11 (.in(main_1_outp[10]));
  LED led_12 (.in(main_1_outp[11]));
  LED led_13 (.in(main_1_outp[12]));
  LED led_14 (.in(main_1_outp[13]));
  LED led_15 (.in(main_1_outp[14]));
  LED led_16 (.in(main_1_outp[15]));
endmodule
