// Logisim project comp_0.2.0.circ as structural Verilog: 11 circuits, main circuit main
module main (
  input  RST
);

  wire clock_1_out, cpu_1_write_m, cpu_1_write_s;
  wire [14:0] cpu_1_address_m, cpu_1_out_pc, cpu_1_out_sp;
  wire [15:0] cpu_1_out_m, memory_1_out_m, memory_1_out_s, rom_1_data;

  ROM #(.addrWidth(15), .dataWidth(16)) rom_1 (.addr(cpu_1_out_pc), .data(rom_1_data));
  Clock clock_1 (.out(clock_1_out));
  CPU cpu_1 (
    .WRITE_S(cpu_1_write_s), .OUT_SP(cpu_1_out_sp), .OUT_M(cpu_1_out_m), .WRITE_M(cpu_1_write_m),
    .ADDRESS_M(cpu_1_address_m), .OUT_PC(cpu_1_out_pc), .RESET(RST), .CLK(clock_1_out),
    .IN_M(memory_1_out_m), .IN_S(memory_1_out_s), .INSTRUCTION(rom_1_data));
  MEMORY memory_1 (
    .OUT_M(memory_1_out_m), .OUT_S(memory_1_out_s), .WRITE_M(cpu_1_write_m), .WRITE_S(cpu_1_write_s),
    .CLK(clock_1_out), .IN_M(cpu_1_out_m), .ADDRESS_M(cpu_1_address_m), .IN_S(cpu_1_out_m),
    .ADDRESS_S(cpu_1_out_sp));

  // Notes on the sheet:
  //   contents of rom_1 (hex, n*v repeats v):
  //   2 c088 c840 e090 c1e0 e910 3 8088 9 cd00 c900 c040 c440 d080 d580 ddb8 8550 8390
endmodule

module CPU (
  input  [15:0] INSTRUCTION,
  input  [15:0] IN_M,
  input  [15:0] IN_S,
  input  RESET,
  input  CLK,
  output [15:0] OUT_M,
  output WRITE_M,
  output [14:0] ADDRESS_M,
  output [14:0] OUT_PC,
  output WRITE_S,
  output [14:0] OUT_SP
);

  wire and_1_out, and_2_out, and_3_out, and_4_out, and_6_out, c_inst_parser_1_a, c_inst_parser_1_a_m,
       c_inst_parser_1_d, c_inst_parser_1_m, c_inst_parser_1_pp, c_inst_parser_1_s, inst_type_1_a,
       inst_type_1_c, jump_decider_1_jmp_bool, not_1_out, or_1_out;
  wire [2:0] c_inst_parser_1_jmp, c_inst_parser_1_oprnd, c_inst_parser_1_oprtr;
  wire [14:0] bit_extender_1_out, sc_1_sp;
  wire [15:0] D_q, multiplexer_1_out, multiplexer_2_out, multiplexer_3_out, multiplexer_4_out,
       selector_1_out1, selector_1_out2;
  wire [15:15] A_q, pc_1_out1;

  Multiplexer #(.enable("false"), .width(16)) multiplexer_1 (
    .in0(INSTRUCTION), .in1(OUT_M), .out(multiplexer_1_out), .sel(inst_type_1_c));
  C_INST_PARSER c_inst_parser_1 (
    .D(c_inst_parser_1_d), .M(c_inst_parser_1_m), .A(c_inst_parser_1_a), .A_M(c_inst_parser_1_a_m),
    .PP(c_inst_parser_1_pp), .S(c_inst_parser_1_s), .OPRND(c_inst_parser_1_oprnd),
    .OPRTR(c_inst_parser_1_oprtr), .JMP(c_inst_parser_1_jmp), .INSTRUCTION(INSTRUCTION));
  INST_TYPE inst_type_1 (.A(inst_type_1_a), .C(inst_type_1_c), .INSTRUCTION(INSTRUCTION));
  and and_1 (and_1_out, c_inst_parser_1_a, inst_type_1_c);
  and and_2 (and_2_out, c_inst_parser_1_d, inst_type_1_c);
  or or_1 (or_1_out, and_1_out, inst_type_1_a);
  Register #(.width(16)) A (.D(multiplexer_1_out), .en(or_1_out), .clk(CLK), .Q({A_q[15], ADDRESS_M}), .clr(RESET));
  Register #(.width(16)) D (.D(OUT_M), .en(and_2_out), .clk(CLK), .Q(D_q), .clr(RESET));
  and and_3 (and_3_out, c_inst_parser_1_s, c_inst_parser_1_pp);
  Multiplexer #(.enable("false"), .width(16)) multiplexer_2 (
    .in0({A_q[15], ADDRESS_M}), .in1(IN_M), .out(multiplexer_2_out), .sel(c_inst_parser_1_a_m));
  Multiplexer #(.enable("false"), .width(16)) multiplexer_3 (
    .in0(multiplexer_2_out), .in1(IN_S), .out(multiplexer_3_out), .sel(and_3_out));
  Multiplexer #(.enable("false"), .width(16)) multiplexer_4 (
    .in0({A_q[15], ADDRESS_M}), .in1(OUT_M), .out(multiplexer_4_out), .sel(c_inst_parser_1_a));
  SC sc_1 (.SP(sc_1_sp), .CLK(CLK), .RESET(RESET), .PUSH_POP(c_inst_parser_1_pp), .ENABLE(c_inst_parser_1_s));
  JUMP_DECIDER jump_decider_1 (.JMP_BOOL(jump_decider_1_jmp_bool), .ALU_OUT(OUT_M), .JMP_SEL(c_inst_parser_1_jmp));
  SC sc_2 ();  // open: SP, CLK, RESET, PUSH_POP, ENABLE
  SELECTOR selector_1 (
    .OUT1(selector_1_out1), .OUT2(selector_1_out2), .OPERAND_SEL(c_inst_parser_1_oprnd), .D(D_q),
    .A(multiplexer_3_out));
  and and_4 (and_4_out, jump_decider_1_jmp_bool, inst_type_1_c);
  not not_1 (not_1_out, c_inst_parser_1_pp);
  and and_5 (WRITE_S, inst_type_1_c, not_1_out, c_inst_parser_1_s);
  and and_6 (and_6_out, inst_type_1_c, c_inst_parser_1_pp, c_inst_parser_1_s);
  PC pc_1 (.OUT1({pc_1_out1[15], OUT_PC}), .LOAD(and_4_out), .RESET(RESET), .CLK(CLK), .IN1(multiplexer_4_out));
  assign bit_extender_1_out = {{14{1'b0}}, and_6_out};  // Bit_Extender bit_extender_1
  and and_7 (WRITE_M, c_inst_parser_1_m, inst_type_1_c);
  ALU alu_1 (.IN1(selector_1_out1), .IN2(selector_1_out2), .SEL(c_inst_parser_1_oprtr), .OUT1(OUT_M));
  Subtractor #(.width(15)) subtractor_1 (.a(sc_1_sp), .b(bit_extender_1_out), .out(OUT_SP));  // open: bin, bout
endmodule

module ALU (
  input  [15:0] IN1,
  input  [15:0] IN2,
  input  [2:0] SEL,
  output [15:0] OUT1
);

  wire [15:0] adder_1_out, and_1_out, divider_1_out, multiplier_1_out, not_1_out, or_1_out, subtractor_1_out,
       xor_1_out;

  Adder #(.width(16)) adder_1 (.a(IN1), .b(IN2), .out(adder_1_out));  // open: cin, cout
  Subtractor #(.width(16)) subtractor_1 (.a(IN1), .b(IN2), .out(subtractor_1_out));  // open: bin, bout
  Multiplier #(.width(16)) multiplier_1 (.a(IN1), .b(IN2), .out(multiplier_1_out));  // open: cin, cout
  Divider #(.width(16)) divider_1 (.a(IN1), .b(IN2), .out(divider_1_out));  // open: upper, rem
  assign not_1_out = ~IN2;  // NOT_Gate not_1, 16 bits wide
  assign and_1_out = IN1 & IN2;  // AND_Gate and_1, 16 bits wide
  assign or_1_out = IN1 | IN2;  // OR_Gate or_1, 16 bits wide
  assign xor_1_out = IN1 ^ IN2;  // XOR_Gate xor_1, 16 bits wide
  Multiplexer #(.enable("false"), .select(3), .width(16)) multiplexer_1 (
    .in0(adder_1_out), .in1(subtractor_1_out), .in2(multiplier_1_out), .in3(divider_1_out), .in4(not_1_out),
    .in5(and_1_out), .in6(or_1_out), .in7(xor_1_out), .out(OUT1), .sel(SEL));
endmodule

module PC (
  input  LOAD,
  input  RESET,
  input  CLK,
  input  [15:0] IN1,
  output [15:0] OUT1
);

  Counter #(.max('hffff), .width(16)) counter_1 (
    .clr(RESET), .load(LOAD), .up(1'b1), .count(1'b1), .clk(CLK), .D(IN1), .Q(OUT1));  // open: carry
endmodule

module SELECTOR (
  input  [15:0] D,
  input  [15:0] A,
  input  [2:0] OPERAND_SEL,
  output [15:0] OUT1,
  output [15:0] OUT2
);

  Multiplexer #(.enable("false"), .select(3), .width(16)) multiplexer_1 (
    .in0({16{1'b0}}), .in1(D), .in2({16{1'b0}}), .in3({16{1'b0}}), .in4(A), .in5({16{1'b0}}), .in6(A),
    .in7(D), .out(OUT1), .sel(OPERAND_SEL));
  Multiplexer #(.enable("false"), .select(3), .width(16)) multiplexer_2 (
    .in0({16{1'b0}}), .in1(A), .in2(A), .in3(D), .in4(D), .in5(16'h1), .in6(16'h1), .in7(16'h1), .out(OUT2),
    .sel(OPERAND_SEL));
endmodule

module INST_TYPE (
  input  [15:0] INSTRUCTION,
  output A,
  output C
);

  not not_1 (A, INSTRUCTION[15]);

  assign C = INSTRUCTION[15];
endmodule

module C_INST_PARSER (
  input  [15:0] INSTRUCTION,
  output [2:0] JMP,
  output D,
  output M,
  output A,
  output [2:0] OPRND,
  output A_M,
  output [2:0] OPRTR,
  output PP,
  output S
);


  assign A = INSTRUCTION[5];
  assign A_M = INSTRUCTION[9];
  assign D = INSTRUCTION[3];
  assign JMP = INSTRUCTION[2:0];
  assign M = INSTRUCTION[4];
  assign OPRND = INSTRUCTION[8:6];
  assign OPRTR = INSTRUCTION[12:10];
  assign PP = INSTRUCTION[13];
  assign S = INSTRUCTION[14];
endmodule

module JUMP_DECIDER (
  input  [2:0] JMP_SEL,
  input  [15:0] ALU_OUT,
  output JMP_BOOL
);

  wire and_1_out, and_2_out, and_3_out, comparator_1_eq, comparator_1_gt, comparator_1_lt;

  Comparator #(.width(16)) comparator_1 (
    .a(ALU_OUT), .b({16{1'b0}}), .gt(comparator_1_gt), .eq(comparator_1_eq), .lt(comparator_1_lt));
  and and_1 (and_1_out, JMP_SEL[0], comparator_1_gt);
  and and_2 (and_2_out, comparator_1_eq, JMP_SEL[1]);
  and and_3 (and_3_out, comparator_1_lt, JMP_SEL[2]);
  or or_1 (JMP_BOOL, and_1_out, and_2_out, and_3_out);
endmodule

module DELAY (
  input  IN1,
  output out_2
);

  wire not_1_out, not_2_out, not_3_out, not_4_out, not_5_out, not_6_out, not_7_out, not_8_out, not_9_out,
       not_10_out, not_11_out, not_12_out, not_13_out, not_14_out, not_15_out, not_16_out, not_17_out,
       not_18_out, not_19_out, not_20_out, not_21_out, not_22_out, not_23_out, not_24_out, not_25_out,
       not_26_out, not_27_out, not_28_out, not_29_out, not_30_out, not_31_out, not_32_out, not_33_out,
       not_34_out, not_35_out, not_36_out, not_37_out, not_38_out, not_39_out, not_40_out, not_41_out,
       not_42_out, not_43_out, not_44_out, not_45_out, not_46_out, not_47_out, not_48_out, not_49_out,
       not_50_out, not_51_out, not_52_out, not_53_out, not_54_out, not_55_out, not_56_out, not_57_out,
       not_58_out, not_59_out, not_60_out, not_61_out, not_62_out, not_63_out;

  not not_1 (not_1_out, IN1);
  not not_2 (not_2_out, not_1_out);
  not not_3 (not_3_out, not_63_out);
  not not_4 (not_4_out, not_3_out);
  not not_5 (not_5_out, not_2_out);
  not not_6 (not_6_out, not_5_out);
  not not_7 (not_7_out, not_4_out);
  not not_8 (not_8_out, not_7_out);
  not not_9 (not_9_out, not_6_out);
  not not_10 (not_10_out, not_9_out);
  not not_11 (not_11_out, not_10_out);
  not not_12 (not_12_out, not_8_out);
  not not_13 (not_13_out, not_12_out);
  not not_14 (not_14_out, not_13_out);
  not not_15 (not_15_out, not_11_out);
  not not_16 (not_16_out, not_15_out);
  not not_17 (not_17_out, not_16_out);
  not not_18 (not_18_out, not_14_out);
  not not_19 (not_19_out, not_18_out);
  not not_20 (not_20_out, not_19_out);
  not not_21 (not_21_out, not_17_out);
  not not_22 (not_22_out, not_21_out);
  not not_23 (not_23_out, not_20_out);
  not not_24 (not_24_out, not_23_out);
  not not_25 (not_25_out, not_22_out);
  not not_26 (not_26_out, not_25_out);
  not not_27 (not_27_out, not_26_out);
  not not_28 (not_28_out, not_24_out);
  not not_29 (not_29_out, not_28_out);
  not not_30 (not_30_out, not_29_out);
  not not_31 (not_31_out, not_27_out);
  not not_32 (not_32_out, not_31_out);
  not not_33 (not_33_out, not_32_out);
  not not_34 (not_34_out, not_30_out);
  not not_35 (not_35_out, not_34_out);
  not not_36 (not_36_out, not_35_out);
  not not_37 (not_37_out, not_33_out);
  not not_38 (not_38_out, not_37_out);
  not not_39 (not_39_out, not_36_out);
  not not_40 (not_40_out, not_39_out);
  not not_41 (not_41_out, not_38_out);
  not not_42 (not_42_out, not_41_out);
  not not_43 (not_43_out, not_42_out);
  not not_44 (not_44_out, not_40_out);
  not not_45 (not_45_out, not_44_out);
  not not_46 (not_46_out, not_45_out);
  not not_47 (not_47_out, not_43_out);
  not not_48 (not_48_out, not_47_out);
  not not_49 (not_49_out, not_48_out);
  not not_50 (not_50_out, not_46_out);
  not not_51 (not_51_out, not_50_out);
  not not_52 (not_52_out, not_51_out);
  not not_53 (not_53_out, not_54_out);
  not not_54 (not_54_out, not_49_out);
  not not_55 (not_55_out, not_56_out);
  not not_56 (not_56_out, not_52_out);
  not not_57 (not_57_out, not_53_out);
  not not_58 (not_58_out, not_57_out);
  not not_59 (not_59_out, not_58_out);
  not not_60 (not_60_out, not_55_out);
  not not_61 (not_61_out, not_60_out);
  not not_62 (not_62_out, not_61_out);
  not not_63 (not_63_out, not_59_out);
  not not_64 (out_2, not_62_out);
endmodule

module SC (
  input  RESET,
  input  PUSH_POP,
  input  ENABLE,
  input  CLK,
  output [14:0] SP
);

  wire not_1_out;

  Counter #(.max('h7fff), .width(15)) counter_1 (
    .clr(RESET), .up(not_1_out), .count(ENABLE), .clk(CLK), .Q(SP));  // open: load, D, carry
  not not_1 (not_1_out, PUSH_POP);
endmodule

module MEMORY (
  input  [15:0] IN_M,
  input  WRITE_M,
  input  [14:0] ADDRESS_M,
  input  [15:0] IN_S,
  input  WRITE_S,
  input  [14:0] ADDRESS_S,
  input  CLK,
  output [15:0] OUT_M,
  output [15:0] OUT_S
);

  RAM #(.addrWidth(15), .dataWidth(16), .enables("line")) ram_1 (
    .addr(ADDRESS_M), .we(WRITE_M), .clk(CLK), .din(IN_M), .dout(OUT_M));
  RAM #(.addrWidth(15), .dataWidth(16), .enables("line")) ram_2 (
    .addr(ADDRESS_S), .we(WRITE_S), .clk(CLK), .din(IN_S), .dout(OUT_S));
endmodule
